# Fritzing sketch RPI_Shutdown (saved by Fritzing 0.9.3b)

parts:
  S1 = Toggle Switch [package=THT]
  D1 = Schottky Diode [part_number=SB560 package="300 mil [THT]"]
  Raspberry_Pi1 = Raspberry Pi B rev2
  U1 = RELAY [part_number=SRD-05VDC-SL-C package=relay-jzc]
  Power_plug1 = Power plug
  R1 = Resistor [tolerance=±5% resistance=100k package=THT]
  2N_3904 = NPN-Transistor [package="TO92 [THT]"]
  C1 = Electrolytic Capacitor [capacitance=1mF package="200 mil [THT, electrolytic]"]  # not connected
  D2 = Schottky Diode [part_number=SB560 package="300 mil [THT]"]

nets:
  N1: S1.COM, Power_plug1.VCC
  GND: S1.L2, D1.anode, Raspberry_Pi1.GPIO_17, R1.Pin_0, R1.Pin_1
  N2: D1.cathode, Raspberry_Pi1.5V, U1.NC, U1.COIL1
  N3: Raspberry_Pi1.GND, 2N_3904.E
  N4: Raspberry_Pi1.GPIO_10, 2N_3904.B
  N5: U1.COIL2, 2N_3904.C, D2.anode
