# Fritzing sketch Wifi_Radio_Wiring (saved by Fritzing 0.9.3b)
breadboards: 1

parts:
  Raspberry_Pi1 = Raspberry Pi B rev2
  Bauteil1 = Arduino Pro Mini v13
  Bauteil2 = Arduino Pro Mini v13
  U1 = LCD-16X2 [package=lcd-16x2]
  Bauteil3 = Logic Level Converter
  Linker_Steuerknopf = Rotary Encoder with Knob
  Rechter_Steuerknopf = Rotary Encoder with Knob
  5_V_/_5I_Netzteil = Power plug
  R1 = Resistor [tolerance=±5% resistance=680 package=THT]
  AMP1 = GF1002 Stereo Amplifier
  SP1 = SPEAKER [package=pcb_mount_speaker]
  SP2 = SPEAKER [package=pcb_mount_speaker]
  U2 = 2.5mm Audio Jack [package=stereojack2.5mm_specia_pogopins]
  S1 = Toggle Switch [package=THT]

nets:
  N1: Raspberry_Pi1.3V3, Raspberry_Pi1.GPIO_24, U1.DB5, Bauteil3.LV
  N2: Raspberry_Pi1.GPIO_3, Rechter_Steuerknopf.no_name_yet#4
  GND: Raspberry_Pi1.GND, Raspberry_Pi1.GPIO_15, Raspberry_Pi1.GPIO_7, Bauteil1.GND, Bauteil1.RESET, Bauteil2.GND, U1.VSS, U1.VO, U1.RS, U1.R_W, U1.K, Bauteil3.RX2_LV, Bauteil3.GND, Linker_Steuerknopf.no_name_yet#2, Linker_Steuerknopf.no_name_yet#5, Rechter_Steuerknopf.no_name_yet#2, Rechter_Steuerknopf.no_name_yet#5
  N3: Raspberry_Pi1.GPIO_23, U1.DB6
  N4: Raspberry_Pi1.GPIO_14, Raspberry_Pi1.GPIO_4, Bauteil3.TX2_LV
  N5: Raspberry_Pi1.GPIO_17, Raspberry_Pi1.GPIO_18, U1.DB7, S1.L1
  N6: Raspberry_Pi1.GPIO_27, Bauteil3.RX_LV
  N7: Raspberry_Pi1.GPIO_22, Bauteil3.TX_LV
  N8: Raspberry_Pi1.GPIO_9, Raspberry_Pi1.GPIO_25, U1.DB4
  N9: Raspberry_Pi1.GPIO_11, Raspberry_Pi1.GPIO_8, U1.E
  VCC: Bauteil1.VCC, Bauteil2.VCC, U1.VDD, Bauteil3.HV, 5_V_/_5I_Netzteil.VCC, R1.Pin_0, AMP1.POWER+
  N10: Bauteil1.A3, Linker_Steuerknopf.no_name_yet#1
  N11: Bauteil1.A2, Linker_Steuerknopf.no_name_yet#3
  N12: Bauteil1.A1, Linker_Steuerknopf.no_name_yet#4
  N13: Bauteil1.D1/RX, Bauteil3.TX2_HV
  N14: Bauteil1.D0/TX, Bauteil3.RX2_HV
  N15: Bauteil2.A3, Rechter_Steuerknopf.no_name_yet#3
  N16: Bauteil2.A2, Rechter_Steuerknopf.no_name_yet#1
  N17: Bauteil2.A1, Bauteil3.RX_HV
  N18: Bauteil2.A0, Bauteil3.TX_HV
  N19: U1.A, R1.Pin_1
  N20: 5_V_/_5I_Netzteil.GND, AMP1.POWER-
  N21: AMP1.ROUT-, SP1.-
  N22: AMP1.ROUT+, SP1.+
  N23: AMP1.LOUT+, SP2.-
  N24: AMP1.LOUT-, SP2.+
  N25: AMP1.INPUTL, U2.RIGHT
  N26: AMP1.INPUTG, U2.SLEEVE
  N27: AMP1.INPUTR, U2.LEFT

custom parts:
  Rotary Encoder with Knob: Rotary Encoder with 1/4" Shaft and Knob
  GF1002 Stereo Amplifier: GF1002 6 Watt Stereo Amplifier
